// Logisim project e2546794.circ as structural Verilog: 1 circuit, main circuit main
module main (
  input  A1,
  input  A0,
  input  B1,
  input  B0,
  output Y,
  output Q,
  output X,
  output Z
);

  wire and_1_out, and_2_out, and_3_out, and_5_out, and_6_out, and_7_out, and_9_out, and_10_out, and_11_out,
       and_12_out, and_13_out, and_14_out, and_15_out, and_16_out, not_1_out, not_2_out, not_3_out,
       not_4_out, or_1_out, or_2_out, or_3_out, or_4_out, or_5_out, or_6_out, or_7_out, or_8_out, or_9_out,
       or_10_out, or_11_out, or_12_out, or_14_out, or_15_out, or_16_out, or_17_out, or_18_out, or_19_out,
       or_20_out, or_21_out, or_22_out;

  not not_1 (not_1_out, A1);
  or or_1 (or_1_out, not_2_out, not_3_out);
  or or_2 (or_2_out, B1, A0);
  or or_3 (or_3_out, A1, or_1_out);
  and and_1 (and_1_out, or_3_out, or_2_out);
  or or_4 (or_4_out, not_2_out, not_3_out);
  or or_5 (or_5_out, or_4_out, B0);
  and and_2 (and_2_out, and_1_out, or_5_out);
  or or_6 (or_6_out, not_1_out, A0);
  or or_7 (or_7_out, not_1_out, B1);
  or or_8 (or_8_out, or_6_out, not_4_out);
  or or_9 (or_9_out, not_4_out, or_7_out);
  and and_3 (and_3_out, and_2_out, or_8_out);
  and and_4 (X, and_3_out, or_9_out);
  not not_2 (not_2_out, A0);
  or or_10 (or_10_out, B0, or_14_out);
  and and_5 (and_5_out, A1, not_3_out);
  and and_6 (and_6_out, not_2_out, not_1_out);
  and and_7 (and_7_out, and_6_out, B1);
  or or_11 (or_11_out, and_5_out, and_7_out);
  or or_12 (or_12_out, or_11_out, and_10_out);
  or or_13 (Z, or_12_out, or_17_out);
  or or_14 (or_14_out, not_2_out, not_1_out);
  or or_15 (or_15_out, not_1_out, B1);
  and and_8 (Y, or_10_out, and_11_out);
  and and_9 (and_9_out, not_2_out, not_1_out);
  and and_10 (and_10_out, and_9_out, B0);
  or or_16 (or_16_out, B1, B0);
  and and_11 (and_11_out, or_15_out, or_16_out);
  and and_12 (and_12_out, not_3_out, not_4_out);
  and and_13 (and_13_out, A0, and_12_out);
  and and_14 (and_14_out, A1, A0);
  and and_15 (and_15_out, not_4_out, and_14_out);
  or or_17 (or_17_out, and_15_out, and_13_out);
  not not_3 (not_3_out, B1);
  or or_18 (or_18_out, not_3_out, A1);
  or or_19 (or_19_out, A1, not_4_out);
  or or_20 (or_20_out, or_19_out, A0);
  and and_16 (and_16_out, or_18_out, or_20_out);
  and and_17 (Q, and_16_out, or_21_out);
  or or_21 (or_21_out, not_3_out, or_22_out);
  not not_4 (not_4_out, B0);
  or or_22 (or_22_out, A0, not_4_out);
endmodule
