// Logisim project e2546794.circ as structural Verilog: 1 circuit, main circuit main
module main (
  input  O3,
  input  O0,
  input  O1,
  input  O2,
  input  A1,
  input  A0,
  input  B1,
  input  B0,
  output E,
  output G,
  output L,
  output L5,
  output C,
  output S,
  output Z,
  output L0,
  output L4,
  output L6,
  output P,
  output L9,
  output L1,
  output L8,
  output L7,
  output L3,
  output L2
);

  wire and_1_out, and_2_out, and_3_out, and_4_out, and_5_out, and_6_out, and_7_out, and_8_out, and_9_out,
       and_10_out, and_11_out, and_13_out, and_14_out, and_15_out, and_16_out, and_17_out, and_18_out,
       and_19_out, and_20_out, and_21_out, and_22_out, and_23_out, and_24_out, and_25_out, and_26_out,
       and_27_out, and_28_out, and_29_out, and_30_out, and_32_out, and_34_out, and_35_out, and_36_out,
       and_38_out, and_39_out, and_40_out, and_41_out, and_42_out, and_43_out, and_44_out, and_46_out,
       and_47_out, and_48_out, and_49_out, and_50_out, n3_to_8_decoder_74138_1_p4,
       n3_to_8_decoder_74138_1_p7, n3_to_8_decoder_74138_1_p8, n3_to_8_decoder_74138_1_p9,
       n3_to_8_decoder_74138_1_p10, n3_to_8_decoder_74138_1_p11, n3_to_8_decoder_74138_1_p12,
       n3_to_8_decoder_74138_1_p13, n3_to_8_decoder_74138_1_p14, n3_to_8_decoder_74138_2_p7,
       n3_to_8_decoder_74138_2_p8, n3_to_8_decoder_74138_2_p9, n3_to_8_decoder_74138_2_p10,
       n3_to_8_decoder_74138_2_p11, n3_to_8_decoder_74138_2_p12, n3_to_8_decoder_74138_2_p13,
       n3_to_8_decoder_74138_2_p14, n3_to_8_decoder_74138_3_p7, n3_to_8_decoder_74138_3_p8,
       n3_to_8_decoder_74138_3_p9, n3_to_8_decoder_74138_3_p10, n3_to_8_decoder_74138_3_p11,
       n3_to_8_decoder_74138_3_p12, n3_to_8_decoder_74138_3_p13, n3_to_8_decoder_74138_3_p14,
       n3_to_8_decoder_74138_4_p7, n3_to_8_decoder_74138_4_p8, n3_to_8_decoder_74138_4_p9,
       n3_to_8_decoder_74138_4_p10, n3_to_8_decoder_74138_4_p11, n3_to_8_decoder_74138_4_p12,
       n3_to_8_decoder_74138_4_p13, n3_to_8_decoder_74138_4_p14, n3_to_8_decoder_74138_5_p2,
       n3_to_8_decoder_74138_5_p7, n3_to_8_decoder_74138_5_p8, n3_to_8_decoder_74138_5_p9,
       n3_to_8_decoder_74138_5_p10, n3_to_8_decoder_74138_5_p11, n3_to_8_decoder_74138_5_p12,
       n3_to_8_decoder_74138_5_p13, n3_to_8_decoder_74138_5_p14, n3_to_8_decoder_74138_6_p1,
       n3_to_8_decoder_74138_6_p7, n3_to_8_decoder_74138_6_p8, n3_to_8_decoder_74138_6_p9,
       n3_to_8_decoder_74138_6_p10, n3_to_8_decoder_74138_6_p11, n3_to_8_decoder_74138_6_p12,
       n3_to_8_decoder_74138_6_p13, n3_to_8_decoder_74138_6_p14, n3_to_8_decoder_74138_7_p4,
       n3_to_8_decoder_74138_7_p5, n3_to_8_decoder_74138_7_p6, n3_to_8_decoder_74138_7_p7,
       n3_to_8_decoder_74138_7_p8, n3_to_8_decoder_74138_7_p9, n3_to_8_decoder_74138_7_p10,
       n3_to_8_decoder_74138_7_p11, n3_to_8_decoder_74138_8_p7, n3_to_8_decoder_74138_8_p8,
       n3_to_8_decoder_74138_8_p9, n3_to_8_decoder_74138_8_p10, n3_to_8_decoder_74138_8_p11,
       n3_to_8_decoder_74138_8_p12, n3_to_8_decoder_74138_8_p13, n3_to_8_decoder_74138_8_p14,
       n3_to_8_decoder_74138_9_p10, n3_to_8_decoder_74138_9_p11, n3_to_8_decoder_74138_9_p12,
       n3_to_8_decoder_74138_9_p13, n3_to_8_decoder_74138_9_p14, n3_to_8_decoder_74138_9_p15,
       n3_to_8_decoder_74138_9_p16, n3_to_8_decoder_74138_9_p17, not_1_out, not_2_out, not_4_out, not_5_out,
       not_6_out, not_7_out, not_8_out, not_9_out, not_10_out, not_11_out, not_12_out, not_13_out,
       not_14_out, not_15_out, not_16_out, not_17_out, not_18_out, not_19_out, not_20_out, not_21_out,
       not_22_out, not_23_out, not_24_out, not_26_out, not_27_out, not_28_out, not_29_out, not_30_out,
       not_31_out, not_32_out, not_33_out, not_34_out, not_35_out, not_36_out, not_38_out, not_39_out,
       not_40_out, not_41_out, not_42_out, not_43_out, not_44_out, not_45_out, not_46_out, not_47_out,
       not_48_out, not_49_out, not_50_out, not_51_out, not_52_out, not_53_out, not_54_out, not_55_out,
       not_56_out, not_57_out, not_58_out, not_59_out, not_60_out, not_61_out, not_62_out, not_63_out,
       not_64_out, not_65_out, not_66_out, not_67_out, not_68_out, not_69_out, not_70_out, not_71_out,
       not_72_out, not_73_out, not_74_out, not_75_out, not_76_out, not_77_out, not_78_out, not_79_out,
       not_80_out, not_81_out, not_82_out, not_83_out, not_84_out, not_85_out, not_86_out, not_87_out,
       not_88_out, not_89_out, not_90_out, not_91_out, not_92_out, not_93_out, not_94_out, not_95_out,
       not_96_out, or_1_out, or_2_out, or_3_out, or_4_out, or_5_out, or_6_out, or_7_out, or_8_out, or_9_out,
       or_10_out, or_11_out, or_12_out, or_13_out, or_14_out, or_15_out, or_18_out, or_20_out, or_21_out,
       or_23_out, or_24_out, or_25_out, or_26_out, or_27_out, or_28_out, or_29_out, or_30_out, or_31_out,
       or_32_out, or_33_out, or_35_out, or_36_out, or_37_out, or_38_out, or_39_out, or_40_out, or_41_out,
       or_42_out, or_43_out, or_44_out, or_46_out, or_47_out, or_48_out, or_49_out, or_50_out, or_51_out,
       or_52_out, or_53_out, or_54_out, or_56_out, xor_1_out, xor_2_out, xor_3_out, xor_5_out, xor_6_out;

  not not_1 (not_1_out, A0);
  not not_2 (not_2_out, B1);
  // _3_to_8_decoder__74138 #(.Facing("east")) 3_to_8_decoder_74138_1: pin names not known; wires that end beside it: O0, O1, O2, n3_to_8_decoder_74138_1_p4, 1'b0, 1'b0, n3_to_8_decoder_74138_1_p7, n3_to_8_decoder_74138_1_p8, n3_to_8_decoder_74138_1_p9, n3_to_8_decoder_74138_1_p10, n3_to_8_decoder_74138_1_p11, n3_to_8_decoder_74138_1_p12, n3_to_8_decoder_74138_1_p13, n3_to_8_decoder_74138_1_p14
  not not_3 (n3_to_8_decoder_74138_1_p4, O3);
  and and_1 (and_1_out, B1, A1);
  and and_2 (and_2_out, B1, B0);
  not not_4 (not_4_out, A1);
  and and_3 (and_3_out, B0, A1);
  xor xor_1 (xor_1_out, A0, B0);
  and and_4 (and_4_out, A0, B0);
  xor xor_2 (xor_2_out, A1, B1);
  and and_5 (and_5_out, A1, B1);
  and and_6 (and_6_out, B0, A0);
  and and_7 (and_7_out, B1, A0);
  and and_8 (and_8_out, and_2_out, not_1_out);
  and and_9 (and_9_out, and_2_out, not_4_out);
  and and_10 (and_10_out, not_2_out, and_3_out);
  not not_5 (not_5_out, n3_to_8_decoder_74138_1_p7);
  not not_6 (not_6_out, n3_to_8_decoder_74138_1_p8);
  not not_7 (not_7_out, n3_to_8_decoder_74138_1_p9);
  not not_8 (not_8_out, n3_to_8_decoder_74138_1_p10);
  not not_9 (not_9_out, n3_to_8_decoder_74138_1_p11);
  not not_10 (not_10_out, n3_to_8_decoder_74138_1_p12);
  not not_11 (not_11_out, n3_to_8_decoder_74138_1_p13);
  not not_12 (not_12_out, n3_to_8_decoder_74138_1_p14);
  xor xor_3 (xor_3_out, and_4_out, xor_2_out);
  and and_11 (and_11_out, and_4_out, xor_2_out);
  or or_1 (or_1_out, and_6_out, and_9_out);
  or or_2 (or_2_out, and_7_out, and_8_out);
  or or_3 (or_3_out, and_11_out, and_5_out);
  or or_4 (or_4_out, or_2_out, and_10_out);
  and and_12 (C, or_3_out, not_8_out);
  // _3_to_8_decoder__74138 #(.Facing("east")) 3_to_8_decoder_74138_2: pin names not known; wires that end beside it: or_1_out, or_4_out, and_1_out, not_6_out, 1'b0, 1'b0, n3_to_8_decoder_74138_2_p7, n3_to_8_decoder_74138_2_p8, n3_to_8_decoder_74138_2_p9, n3_to_8_decoder_74138_2_p10, n3_to_8_decoder_74138_2_p11, n3_to_8_decoder_74138_2_p12, n3_to_8_decoder_74138_2_p13, n3_to_8_decoder_74138_2_p14
  not not_13 (not_13_out, A1);
  and and_13 (and_13_out, not_13_out, A0);
  and and_14 (and_14_out, A0, not_14_out);
  not not_14 (not_14_out, B1);
  and and_15 (and_15_out, A0, A1);
  not not_15 (not_15_out, B0);
  and and_16 (and_16_out, B1, A1);
  // _3_to_8_decoder__74138 #(.Facing("east")) 3_to_8_decoder_74138_3: pin names not known; wires that end beside it: xor_1_out, xor_3_out, or_3_out, not_8_out, 1'b0, 1'b0, n3_to_8_decoder_74138_3_p7, n3_to_8_decoder_74138_3_p8, n3_to_8_decoder_74138_3_p9, n3_to_8_decoder_74138_3_p10, n3_to_8_decoder_74138_3_p11, n3_to_8_decoder_74138_3_p12, n3_to_8_decoder_74138_3_p13, n3_to_8_decoder_74138_3_p14, B0
  not not_16 (not_16_out, A1);
  not not_17 (not_17_out, A0);
  and and_17 (and_17_out, B1, A0);
  not not_18 (not_18_out, B0);
  and and_18 (and_18_out, and_13_out, B1);
  not not_19 (not_19_out, A0);
  and and_19 (and_19_out, B0, and_20_out);
  and and_20 (and_20_out, B1, A1);
  and and_21 (and_21_out, not_15_out, and_16_out);
  not not_20 (not_20_out, n3_to_8_decoder_74138_3_p7);
  not not_21 (not_21_out, n3_to_8_decoder_74138_3_p8);
  not not_22 (not_22_out, n3_to_8_decoder_74138_3_p9);
  not not_23 (not_23_out, n3_to_8_decoder_74138_3_p10);
  not not_24 (not_24_out, n3_to_8_decoder_74138_3_p11);
  not not_25 (L5, n3_to_8_decoder_74138_3_p12);
  not not_26 (not_26_out, n3_to_8_decoder_74138_3_p13);
  not not_27 (not_27_out, n3_to_8_decoder_74138_3_p14);
  or or_5 (or_5_out, B1, A1);
  not not_28 (not_28_out, B1);
  or or_6 (or_6_out, not_28_out, not_16_out);
  not not_29 (not_29_out, B0);
  or or_7 (or_7_out, not_16_out, A0);
  and and_22 (and_22_out, not_16_out, B1);
  and and_23 (and_23_out, not_16_out, B0);
  and and_24 (and_24_out, B1, not_17_out);
  not not_30 (not_30_out, n3_to_8_decoder_74138_2_p7);
  not not_31 (not_31_out, n3_to_8_decoder_74138_2_p8);
  not not_32 (not_32_out, n3_to_8_decoder_74138_2_p9);
  not not_33 (not_33_out, n3_to_8_decoder_74138_2_p10);
  not not_34 (not_34_out, n3_to_8_decoder_74138_2_p11);
  not not_35 (not_35_out, n3_to_8_decoder_74138_2_p12);
  not not_36 (not_36_out, n3_to_8_decoder_74138_2_p13);
  not not_37 (L9, n3_to_8_decoder_74138_2_p14);
  and and_25 (and_25_out, and_17_out, not_18_out);
  and and_26 (and_26_out, not_19_out, and_19_out);
  or or_8 (or_8_out, and_14_out, or_9_out);
  or or_9 (or_9_out, and_15_out, and_21_out);
  and and_27 (and_27_out, or_5_out, or_6_out);
  not not_38 (not_38_out, B1);
  and and_28 (and_28_out, and_27_out, or_10_out);
  or or_10 (or_10_out, not_29_out, or_7_out);
  or or_11 (or_11_out, and_22_out, and_29_out);
  and and_29 (and_29_out, and_23_out, not_17_out);
  and and_30 (and_30_out, and_24_out, B0);
  or or_12 (or_12_out, and_25_out, and_18_out);
  not not_39 (not_39_out, B1);
  or or_13 (or_13_out, not_40_out, or_14_out);
  not not_40 (not_40_out, A0);
  or or_14 (or_14_out, B0, not_38_out);
  or or_15 (or_15_out, or_11_out, and_30_out);
  // _3_to_8_decoder__74138 #(.Facing("east")) 3_to_8_decoder_74138_4: pin names not known; wires that end beside it: or_12_out, and_26_out, 1'b0, not_5_out, 1'b0, 1'b0, n3_to_8_decoder_74138_4_p7, n3_to_8_decoder_74138_4_p8, n3_to_8_decoder_74138_4_p9, n3_to_8_decoder_74138_4_p10, n3_to_8_decoder_74138_4_p11, n3_to_8_decoder_74138_4_p12, n3_to_8_decoder_74138_4_p13, n3_to_8_decoder_74138_4_p14
  // _3_to_8_decoder__74138 #(.Facing("east")) 3_to_8_decoder_74138_5: pin names not known; wires that end beside it: or_8_out, n3_to_8_decoder_74138_5_p2, 1'b0, not_7_out, 1'b0, 1'b0, n3_to_8_decoder_74138_5_p7, n3_to_8_decoder_74138_5_p8, n3_to_8_decoder_74138_5_p9, n3_to_8_decoder_74138_5_p10, n3_to_8_decoder_74138_5_p11, n3_to_8_decoder_74138_5_p12, n3_to_8_decoder_74138_5_p13, n3_to_8_decoder_74138_5_p14
  and and_31 (n3_to_8_decoder_74138_5_p2, A1, not_39_out);
  and and_32 (and_32_out, or_13_out, and_28_out);
  and and_33 (S, not_9_out, or_15_out);
  or or_16 (L4, not_34_out, not_24_out);
  or or_17 (L6, not_36_out, not_26_out);
  not not_41 (not_41_out, n3_to_8_decoder_74138_4_p7);
  not not_42 (not_42_out, n3_to_8_decoder_74138_4_p8);
  not not_43 (not_43_out, n3_to_8_decoder_74138_4_p9);
  not not_44 (not_44_out, n3_to_8_decoder_74138_4_p10);
  not not_45 (not_45_out, n3_to_8_decoder_74138_4_p11);
  not not_46 (not_46_out, n3_to_8_decoder_74138_4_p12);
  not not_47 (not_47_out, n3_to_8_decoder_74138_4_p13);
  not not_48 (not_48_out, n3_to_8_decoder_74138_4_p14);
  not not_49 (not_49_out, n3_to_8_decoder_74138_5_p7);
  not not_50 (not_50_out, n3_to_8_decoder_74138_5_p8);
  not not_51 (not_51_out, n3_to_8_decoder_74138_5_p9);
  not not_52 (not_52_out, n3_to_8_decoder_74138_5_p10);
  not not_53 (not_53_out, n3_to_8_decoder_74138_5_p11);
  not not_54 (not_54_out, n3_to_8_decoder_74138_5_p12);
  not not_55 (not_55_out, n3_to_8_decoder_74138_5_p13);
  not not_56 (not_56_out, n3_to_8_decoder_74138_5_p14);
  // _3_to_8_decoder__74138 #(.Facing("east")) 3_to_8_decoder_74138_6: pin names not known; wires that end beside it: n3_to_8_decoder_74138_6_p1, and_32_out, 1'b0, not_9_out, 1'b0, 1'b0, n3_to_8_decoder_74138_6_p7, n3_to_8_decoder_74138_6_p8, n3_to_8_decoder_74138_6_p9, n3_to_8_decoder_74138_6_p10, n3_to_8_decoder_74138_6_p11, n3_to_8_decoder_74138_6_p12, n3_to_8_decoder_74138_6_p13, n3_to_8_decoder_74138_6_p14
  xor xor_4 (n3_to_8_decoder_74138_6_p1, B0, A0);
  or or_18 (or_18_out, L1, L4);
  or or_19 (P, L2, or_18_out);
  not not_57 (not_57_out, n3_to_8_decoder_74138_6_p7);
  not not_58 (not_58_out, n3_to_8_decoder_74138_6_p8);
  not not_59 (not_59_out, n3_to_8_decoder_74138_6_p9);
  not not_60 (not_60_out, n3_to_8_decoder_74138_6_p10);
  not not_61 (not_61_out, n3_to_8_decoder_74138_6_p11);
  not not_62 (not_62_out, n3_to_8_decoder_74138_6_p12);
  not not_63 (not_63_out, n3_to_8_decoder_74138_6_p13);
  not not_64 (not_64_out, n3_to_8_decoder_74138_6_p14);
  and and_34 (and_34_out, and_35_out, or_23_out);
  and and_35 (and_35_out, and_36_out, or_24_out);
  and and_36 (and_36_out, or_21_out, or_20_out);
  or or_20 (or_20_out, not_66_out, B0);
  or or_21 (or_21_out, not_65_out, B1);
  not not_65 (not_65_out, A1);
  not not_66 (not_66_out, A0);
  or or_22 (L0, or_30_out, not_30_out);
  or or_23 (or_23_out, A0, not_68_out);
  or or_24 (or_24_out, A1, not_67_out);
  not not_67 (not_67_out, B1);
  not not_68 (not_68_out, B0);
  or or_25 (or_25_out, not_57_out, not_49_out);
  or or_26 (or_26_out, not_87_out, or_25_out);
  or or_27 (or_27_out, not_79_out, or_26_out);
  or or_28 (or_28_out, not_71_out, or_27_out);
  or or_29 (or_29_out, not_20_out, or_28_out);
  or or_30 (or_30_out, not_41_out, or_29_out);
  and and_37 (E, and_34_out, not_10_out);
  and and_38 (and_38_out, A1, B1);
  or or_31 (or_31_out, A1, B1);
  xor xor_5 (xor_5_out, A1, B1);
  or or_32 (or_32_out, not_23_out, or_38_out);
  or or_33 (or_33_out, not_60_out, or_32_out);
  or or_34 (L3, not_52_out, or_33_out);
  and and_39 (and_39_out, A0, B0);
  or or_35 (or_35_out, A0, B0);
  xor xor_6 (xor_6_out, A0, B0);
  or or_36 (or_36_out, not_82_out, not_90_out);
  or or_37 (or_37_out, not_74_out, or_36_out);
  or or_38 (or_38_out, not_33_out, or_37_out);
  and and_40 (and_40_out, A1, not_69_out);
  not not_69 (not_69_out, B1);
  // _3_to_8_decoder__74138 #(.Facing("east")) 3_to_8_decoder_74138_7: pin names not known; wires that end beside it: and_39_out, and_38_out, 1'b0, n3_to_8_decoder_74138_7_p4, n3_to_8_decoder_74138_7_p5, n3_to_8_decoder_74138_7_p6, n3_to_8_decoder_74138_7_p7, n3_to_8_decoder_74138_7_p8, n3_to_8_decoder_74138_7_p9, n3_to_8_decoder_74138_7_p10, n3_to_8_decoder_74138_7_p11
  // _3_to_8_decoder__74138 #(.Facing("east")) 3_to_8_decoder_74138_8: pin names not known; wires that end beside it: or_35_out, or_31_out, 1'b0, not_11_out, 1'b0, 1'b0, n3_to_8_decoder_74138_8_p7, n3_to_8_decoder_74138_8_p8, n3_to_8_decoder_74138_8_p9, n3_to_8_decoder_74138_8_p10, n3_to_8_decoder_74138_8_p11, n3_to_8_decoder_74138_8_p12, n3_to_8_decoder_74138_8_p13, n3_to_8_decoder_74138_8_p14
  // _3_to_8_decoder__74138 #(.Facing("east")) 3_to_8_decoder_74138_9: pin names not known; wires that end beside it: O3, xor_6_out, xor_5_out, 1'b0, 1'b0, not_12_out, 1'b0, 1'b0, 1'b0, n3_to_8_decoder_74138_9_p10, n3_to_8_decoder_74138_9_p11, n3_to_8_decoder_74138_9_p12, n3_to_8_decoder_74138_9_p13, n3_to_8_decoder_74138_9_p14, n3_to_8_decoder_74138_9_p15, n3_to_8_decoder_74138_9_p16, n3_to_8_decoder_74138_9_p17
  or or_39 (or_39_out, or_40_out, and_41_out);
  or or_40 (or_40_out, and_40_out, and_42_out);
  and and_41 (and_41_out, and_43_out, A0);
  and and_42 (and_42_out, and_44_out, A0);
  and and_43 (and_43_out, not_70_out, A1);
  and and_44 (and_44_out, not_69_out, not_70_out);
  not not_70 (not_70_out, B0);
  or or_41 (or_41_out, not_59_out, or_47_out);
  or or_42 (or_42_out, not_32_out, or_41_out);
  or or_43 (or_43_out, not_43_out, or_42_out);
  or or_44 (or_44_out, not_22_out, or_43_out);
  or or_45 (L2, not_51_out, or_44_out);
  not not_71 (not_71_out, n3_to_8_decoder_74138_7_p4);
  not not_72 (not_72_out, n3_to_8_decoder_74138_7_p5);
  not not_73 (not_73_out, n3_to_8_decoder_74138_7_p6);
  not not_74 (not_74_out, n3_to_8_decoder_74138_7_p7);
  not not_75 (not_75_out, n3_to_8_decoder_74138_7_p8);
  not not_76 (not_76_out, n3_to_8_decoder_74138_7_p9);
  not not_77 (not_77_out, n3_to_8_decoder_74138_7_p10);
  not not_78 (not_78_out, n3_to_8_decoder_74138_7_p11);
  not not_79 (not_79_out, n3_to_8_decoder_74138_8_p7);
  not not_80 (not_80_out, n3_to_8_decoder_74138_8_p8);
  not not_81 (not_81_out, n3_to_8_decoder_74138_8_p9);
  not not_82 (not_82_out, n3_to_8_decoder_74138_8_p10);
  not not_83 (not_83_out, n3_to_8_decoder_74138_8_p11);
  not not_84 (not_84_out, n3_to_8_decoder_74138_8_p12);
  not not_85 (not_85_out, n3_to_8_decoder_74138_8_p13);
  not not_86 (not_86_out, n3_to_8_decoder_74138_8_p14);
  not not_87 (not_87_out, n3_to_8_decoder_74138_9_p10);
  not not_88 (not_88_out, n3_to_8_decoder_74138_9_p11);
  not not_89 (not_89_out, n3_to_8_decoder_74138_9_p12);
  not not_90 (not_90_out, n3_to_8_decoder_74138_9_p13);
  not not_91 (not_91_out, n3_to_8_decoder_74138_9_p14);
  not not_92 (not_92_out, n3_to_8_decoder_74138_9_p15);
  not not_93 (not_93_out, n3_to_8_decoder_74138_9_p16);
  not not_94 (not_94_out, n3_to_8_decoder_74138_9_p17);
  or or_46 (or_46_out, not_81_out, not_73_out);
  or or_47 (or_47_out, not_89_out, or_46_out);
  and and_45 (G, or_39_out, not_10_out);
  or or_48 (or_48_out, and_47_out, and_48_out);
  and and_46 (and_46_out, not_95_out, not_96_out);
  and and_47 (and_47_out, not_95_out, B1);
  not not_95 (not_95_out, A1);
  or or_49 (or_49_out, not_21_out, not_58_out);
  or or_50 (or_50_out, not_50_out, or_49_out);
  or or_51 (or_51_out, not_72_out, or_50_out);
  or or_52 (or_52_out, not_80_out, or_51_out);
  or or_53 (or_53_out, not_88_out, or_52_out);
  or or_54 (or_54_out, not_42_out, or_53_out);
  or or_55 (L1, not_31_out, or_54_out);
  and and_48 (and_48_out, and_46_out, B0);
  not not_96 (not_96_out, A0);
  or or_56 (or_56_out, or_48_out, and_49_out);
  and and_49 (and_49_out, not_96_out, and_50_out);
  and and_50 (and_50_out, B1, B0);
  and and_51 (L, or_56_out, not_10_out);

  assign L7 = 1'b0;
  assign L8 = 1'b0;
  assign Z = L0;
  // also tied to GND on the sheet: {not_35_out, not_27_out, not_44_out, not_45_out, not_46_out, not_47_out, not_48_out, not_53_out, not_54_out, not_55_out, not_56_out, not_61_out, not_62_out, not_63_out, not_64_out, not_75_out, not_76_out, not_77_out, not_78_out, not_83_out, not_84_out, not_85_out, not_86_out, not_91_out, not_92_out, not_93_out, not_94_out}
endmodule
